# Fritzing sketch entrada_analogica (saved by Fritzing 0.9.2b)
breadboards: 1

parts:
  Parte1 = Arduino Uno (Rev3)
  R1 = Rotary Potentiometer (Small) [maximum_resistance=100kΩ package=THT]

nets:
  N1: Parte1.A4/SDA, R1.wiper
  N2: Parte1.5V, R1.leg2
  N3: Parte1.GND, R1.leg1
