# Fritzing sketch entrada_digital (saved by Fritzing 0.9.2b)
breadboards: 1

parts:
  Parte1 = Arduino Uno (Rev3)
  R1 = Resistor [tolerance=±5% resistance=10k package=THT]
  S1 = Pushbutton [package="[THT]"]

nets:
  N1: Parte1.D2, R1.Pin_1, S1.Pin_3, S1.Pin_4
  N2: Parte1.5V, R1.Pin_0
  N3: Parte1.GND, S1.Pin_1, S1.Pin_2
