# Fritzing sketch salida_digital (saved by Fritzing 0.9.2b)
breadboards: 1

parts:
  Parte1 = Arduino Uno (Rev3)
  J1 = Piezo Speaker
  LED1 = LED - 5mm [color="Red (633nm)" package="5 mm [THT]"]
  R1 = Resistor [tolerance=±5% resistance=330 package=THT]
  LED2 = LED - 5mm [color="Red (633nm)" package="5 mm [THT]"]  # not connected
  LED3 = LED - 5mm [color="Red (633nm)" package="5 mm [THT]"]  # not connected
  LED4 = LED - 5mm [color="Red (633nm)" package="5 mm [THT]"]
  R2 = Resistor [tolerance=±5% resistance=330 package=THT]
  R3 = Resistor [tolerance=±5% resistance=330 package=THT]
  R4 = Resistor [tolerance=±5% resistance=330 package=THT]

nets:
  N1: Parte1.GND, J1.pin1, LED1.cathode, LED4.cathode
  N2: Parte1.D3_PWM, R3.Pin_1
  N3: Parte1.D4, R4.Pin_1
  N4: Parte1.D5_PWM, R2.Pin_1
  N5: Parte1.D6_PWM, R1.Pin_1
  N6: Parte1.D7, J1.pin2
  N7: LED1.anode, R1.Pin_0
  N8: LED4.anode, R3.Pin_0
