# Fritzing sketch salida_pwm (saved by Fritzing 0.9.2b)
breadboards: 1

parts:
  Parte1 = Arduino Uno (Rev3)
  LED1 = LED - 5mm [color="Red (633nm)" package="5 mm [THT]"]
  R1 = Resistor [tolerance=±5% resistance=330 package=THT]
  LED2 = RGB LED (com. cathode, rgb) [package="5 mm [THT]"]
  R2 = Resistor [tolerance=±5% resistance=330 package=THT]
  R3 = Resistor [tolerance=±5% resistance=330 package=THT]
  R4 = Resistor [tolerance=±5% resistance=330 package=THT]

nets:
  N1: Parte1.D9_PWM, R3.Pin_1
  N2: Parte1.D10_PWM/SS, R4.Pin_1
  N3: Parte1.D11_PWM/MOSI, R2.Pin_0
  N4: Parte1.GND, LED1.cathode
  N5: Parte1.D6_PWM, R1.Pin_0
  N6: Parte1.5V, LED2.common_cathode
  N7: LED1.anode, R1.Pin_1
  N8: LED2.red_anode, R2.Pin_1
  N9: LED2.green_anode, R4.Pin_0
  N10: LED2.blue_anode, R3.Pin_0
